// Logisim project 1. Decade Counter using JK-Flip Flop.circ as structural Verilog: 2 circuits, main circuit main
module main (
  input  S,
  output [3:0] out_2
);

  wire and_1_out, and_2_out, and_3_out, and_4_out, and_5_out, and_6_out, and_7_out, and_8_out, and_9_out,
       and_10_out, and_11_out, button_1_out, clock_1_out, j_k_ff_1_qn, j_k_ff_2_qn, j_k_ff_3_qn, j_k_ff_4_qn,
       multiplexer_1_out, multiplexer_2_out, multiplexer_3_out, or_1_out, or_2_out, or_3_out;

  Clock clock_1 (.out(clock_1_out));
  Button button_1 (.out(button_1_out));
  J_K_Flip_Flop j_k_ff_1 (
    .J(1'b1), .clk(clock_1_out), .K(1'b1), .Q(out_2[0]), .Qn(j_k_ff_1_qn), .en(button_1_out));  // open: preset, reset
  and and_1 (and_1_out, out_2[0], j_k_ff_4_qn);
  and and_2 (and_2_out, out_2[1], j_k_ff_1_qn);
  and and_3 (and_3_out, out_2[2], j_k_ff_1_qn);
  and and_4 (and_4_out, out_2[3], j_k_ff_1_qn);
  Multiplexer #(.enable("false")) multiplexer_1 (.in0(and_1_out), .in1(or_1_out), .out(multiplexer_1_out), .sel(S));
  or or_1 (or_1_out, and_2_out, and_3_out, and_4_out);
  J_K_Flip_Flop j_k_ff_2 (
    .J(multiplexer_1_out), .clk(clock_1_out), .K(multiplexer_1_out), .Q(out_2[1]), .Qn(j_k_ff_2_qn),
    .en(button_1_out));  // open: preset, reset
  and and_5 (and_5_out, out_2[0], out_2[1]);
  and and_6 (and_6_out, j_k_ff_2_qn, j_k_ff_1_qn);
  and and_7 (and_7_out, out_2[2], and_6_out);
  and and_8 (and_8_out, and_6_out, out_2[3]);
  Multiplexer #(.enable("false")) multiplexer_2 (.in0(and_5_out), .in1(or_2_out), .out(multiplexer_2_out), .sel(S));
  or or_2 (or_2_out, and_7_out, and_8_out);
  J_K_Flip_Flop j_k_ff_3 (
    .J(multiplexer_2_out), .clk(clock_1_out), .K(multiplexer_2_out), .Q(out_2[2]), .Qn(j_k_ff_3_qn),
    .en(button_1_out));  // open: preset, reset
  and and_9 (and_9_out, and_5_out, out_2[2]);
  and and_10 (and_10_out, out_2[0], out_2[3]);
  or or_3 (or_3_out, and_9_out, and_10_out);
  Multiplexer #(.enable("false")) multiplexer_3 (.in0(or_3_out), .in1(and_11_out), .out(multiplexer_3_out), .sel(S));
  and and_11 (and_11_out, j_k_ff_3_qn, j_k_ff_2_qn, j_k_ff_1_qn);
  J_K_Flip_Flop j_k_ff_4 (
    .J(multiplexer_3_out), .clk(clock_1_out), .K(multiplexer_3_out), .Q(out_2[3]), .Qn(j_k_ff_4_qn),
    .en(button_1_out));  // open: preset, reset
endmodule

module Seven_Segment (
  input  A,
  input  B,
  input  C,
  input  D
);

  wire and_1_out, and_2_out, and_3_out, and_4_out, and_5_out, and_6_out, and_7_out, and_8_out, and_9_out,
       and_10_out, and_11_out, and_12_out, and_13_out, and_14_out, and_15_out, and_16_out, and_17_out,
       not_1_out, not_2_out, not_3_out, not_4_out, or_1_out, or_2_out, or_3_out, or_4_out, or_5_out,
       or_6_out, or_7_out, undriven, undriven_2, undriven_3, undriven_4;

  not not_1 (not_1_out, undriven);
  not not_2 (not_2_out, undriven_2);
  not not_3 (not_3_out, undriven_3);
  not not_4 (not_4_out, undriven_4);
  and and_1 (and_1_out, not_1_out, undriven_3);
  and and_2 (and_2_out, undriven, not_2_out, not_3_out);
  and and_3 (and_3_out, not_1_out, not_2_out);
  and and_4 (and_4_out, not_1_out, undriven_3, undriven_4);
  and and_5 (and_5_out, not_1_out, undriven_4);
  and and_6 (and_6_out, undriven, not_2_out, not_3_out);
  and and_7 (and_7_out, not_1_out, not_2_out, undriven_3);
  and and_8 (and_8_out, not_1_out, undriven_2, not_3_out, undriven_4);
  and and_9 (and_9_out, not_1_out, undriven_2, not_3_out);
  and and_10 (and_10_out, not_1_out, undriven_2, not_4_out);
  and and_11 (and_11_out, not_1_out, undriven_2, undriven_4);
  and and_12 (and_12_out, not_2_out, not_3_out, not_4_out);
  and and_13 (and_13_out, not_1_out, not_3_out, not_4_out);
  and and_14 (and_14_out, not_1_out, undriven_2);
  and and_15 (and_15_out, not_1_out, not_2_out, not_3_out);
  and and_16 (and_16_out, undriven, not_2_out, not_3_out);
  and and_17 (and_17_out, not_1_out, undriven_3, not_4_out);
  or or_1 (or_1_out, and_1_out, and_11_out, and_2_out, and_12_out);
  or or_2 (or_2_out, and_2_out, and_3_out, and_13_out, and_4_out);
  or or_3 (or_3_out, and_14_out, and_5_out, and_15_out, and_6_out);
  or or_4 (or_4_out, and_16_out, and_7_out, and_12_out, and_17_out, and_8_out);
  or or_5 (or_5_out, and_12_out, and_17_out);
  or or_6 (or_6_out, and_13_out, and_7_out, and_9_out, and_10_out);
  or or_7 (or_7_out, and_16_out, and_7_out, and_17_out, and_9_out);
  _7_Segment_Display u_7_segment_display_1 ();  // open: g, f, a, b, e, d, c, dp
endmodule
