// Logisim project Cascade.circ as structural Verilog: 4 circuits, main circuit main
module main (
  input  in_1,
  input  S,
  input  C
);

  wire and_1_out, and_2_out, and_3_out, and_4_out, and_5_out, and_6_out, and_7_out, and_8_out, and_9_out,
       and_10_out, and_11_out, j_k_ff_1_qn, j_k_ff_2_qn, j_k_ff_3_qn, j_k_ff_4_qn, multiplexer_1_out,
       multiplexer_2_out, multiplexer_3_out, or_1_out, or_2_out, or_3_out;
  wire [3:0] j_k_ff_1_q;

  J_K_Flip_Flop j_k_ff_1 (
    .J(1'b1), .clk(in_1), .K(1'b1), .Q(j_k_ff_1_q[0]), .Qn(j_k_ff_1_qn), .reset(C));  // open: preset, en
  and and_1 (and_1_out, j_k_ff_1_q[0], j_k_ff_4_qn);
  and and_2 (and_2_out, j_k_ff_1_q[1], j_k_ff_1_qn);
  and and_3 (and_3_out, j_k_ff_1_q[2], j_k_ff_1_qn);
  and and_4 (and_4_out, j_k_ff_1_q[3], j_k_ff_1_qn);
  Multiplexer #(.enable("false")) multiplexer_1 (.in0(and_1_out), .in1(or_1_out), .out(multiplexer_1_out), .sel(S));
  or or_1 (or_1_out, and_2_out, and_3_out, and_4_out);
  J_K_Flip_Flop j_k_ff_2 (
    .J(multiplexer_1_out), .clk(in_1), .K(multiplexer_1_out), .Q(j_k_ff_1_q[1]), .Qn(j_k_ff_2_qn), .reset(C));  // open: preset, en
  and and_5 (and_5_out, j_k_ff_1_q[0], j_k_ff_1_q[1]);
  and and_6 (and_6_out, j_k_ff_2_qn, j_k_ff_1_qn);
  and and_7 (and_7_out, j_k_ff_1_q[2], and_6_out);
  and and_8 (and_8_out, and_6_out, j_k_ff_1_q[3]);
  Multiplexer #(.enable("false")) multiplexer_2 (.in0(and_5_out), .in1(or_2_out), .out(multiplexer_2_out), .sel(S));
  or or_2 (or_2_out, and_7_out, and_8_out);
  J_K_Flip_Flop j_k_ff_3 (
    .J(multiplexer_2_out), .clk(in_1), .K(multiplexer_2_out), .Q(j_k_ff_1_q[2]), .Qn(j_k_ff_3_qn), .reset(C));  // open: preset, en
  and and_9 (and_9_out, and_5_out, j_k_ff_1_q[2]);
  or or_3 (or_3_out, and_9_out, and_10_out);
  and and_10 (and_10_out, j_k_ff_1_q[0], j_k_ff_1_q[3]);
  and and_11 (and_11_out, j_k_ff_3_qn, j_k_ff_2_qn, j_k_ff_1_qn);
  Multiplexer #(.enable("false")) multiplexer_3 (.in0(or_3_out), .in1(and_11_out), .out(multiplexer_3_out), .sel(S));
  J_K_Flip_Flop j_k_ff_4 (
    .J(multiplexer_3_out), .clk(in_1), .K(multiplexer_3_out), .Q(j_k_ff_1_q[3]), .Qn(j_k_ff_4_qn), .reset(C));  // open: preset, en
  Hex_Digit_Display hex_digit_display_1 (.value(j_k_ff_1_q));  // open: dp
endmodule

module cas (
  input  in_1
);

  wire and_1_out, and_2_out, clock_1_out, multiplexer_1_out, not_1_out, not_2_out, not_3_out, not_4_out,
       not_5_out, not_6_out;
  wire [3:0] main_1_p3, main_3_p3;

  Clock clock_1 (.out(clock_1_out));
  // main main_1: pin names not known; wires that end beside it: clock_1_out, in_1, main_1_p3
  not not_1 (not_1_out, main_1_p3[1]);
  not not_2 (not_2_out, main_1_p3[2]);
  not not_3 (not_3_out, main_1_p3[1]);
  not not_4 (not_4_out, main_1_p3[2]);
  not not_5 (not_5_out, main_1_p3[0]);
  not not_6 (not_6_out, main_1_p3[3]);
  main main_2 ();  // open: in_1, S, C
  and and_1 (and_1_out, not_5_out, not_1_out, not_2_out, not_6_out);
  and and_2 (and_2_out, main_1_p3[0], not_3_out, not_4_out, main_1_p3[3]);
  Multiplexer #(.enable("false")) multiplexer_1 (.in0(and_1_out), .in1(and_2_out), .out(multiplexer_1_out), .sel(in_1));
  Hex_Digit_Display hex_digit_display_1 (.value(main_3_p3));  // open: dp
  // main main_3: pin names not known; wires that end beside it: multiplexer_1_out, in_1, main_3_p3
  Hex_Digit_Display hex_digit_display_2 (.value(main_1_p3));  // open: dp
endmodule

module counter6 (
  input  in_1,
  input  S,
  output [2:0] out_3
);

  wire and_1_out, and_2_out, and_3_out, and_4_out, and_5_out, and_6_out, j_k_ff_1_qn, j_k_ff_2_qn,
       j_k_ff_3_qn, multiplexer_1_out, multiplexer_2_out, or_1_out, or_2_out;

  J_K_Flip_Flop j_k_ff_1 (.J(1'b1), .clk(in_1), .K(1'b1), .Q(out_3[0]), .Qn(j_k_ff_1_qn));  // open: preset, en, reset
  and and_1 (and_1_out, out_3[2], j_k_ff_1_qn);
  and and_2 (and_2_out, j_k_ff_1_qn, out_3[1]);
  and and_3 (and_3_out, j_k_ff_3_qn, out_3[0]);
  Multiplexer #(.enable("false")) multiplexer_1 (.in0(and_3_out), .in1(or_1_out), .out(multiplexer_1_out), .sel(S));
  or or_1 (or_1_out, and_1_out, and_2_out);
  J_K_Flip_Flop j_k_ff_2 (
    .J(multiplexer_1_out), .clk(in_1), .K(multiplexer_1_out), .Q(out_3[1]), .Qn(j_k_ff_2_qn));  // open: preset, en, reset
  and and_4 (and_4_out, out_3[2], out_3[0]);
  and and_5 (and_5_out, out_3[0], out_3[1]);
  or or_2 (or_2_out, and_4_out, and_5_out);
  Multiplexer #(.enable("false")) multiplexer_2 (.in0(or_2_out), .in1(and_6_out), .out(multiplexer_2_out), .sel(S));
  and and_6 (and_6_out, j_k_ff_2_qn, j_k_ff_1_qn);
  J_K_Flip_Flop j_k_ff_3 (
    .J(multiplexer_2_out), .clk(in_1), .K(multiplexer_2_out), .Q(out_3[2]), .Qn(j_k_ff_3_qn));  // open: preset, en, reset
endmodule

module minute (
  input  in_1
);

  wire and_1_out, and_2_out, main_1_p1, multiplexer_1_out, not_1_out, not_2_out, not_3_out, not_4_out,
       not_5_out, not_6_out;
  wire [2:0] counter6_1_out_3;
  wire [3:0] main_1_p3;

  // main main_1: pin names not known; wires that end beside it: main_1_p1, in_1, main_1_p3
  Clock clock_1 (.out(main_1_p1));
  not not_1 (not_1_out, main_1_p3[1]);
  not not_2 (not_2_out, main_1_p3[2]);
  not not_3 (not_3_out, main_1_p3[1]);
  not not_4 (not_4_out, main_1_p3[2]);
  not not_5 (not_5_out, main_1_p3[0]);
  not not_6 (not_6_out, main_1_p3[3]);
  and and_1 (and_1_out, not_5_out, not_1_out, not_2_out, not_6_out);
  and and_2 (and_2_out, main_1_p3[0], not_3_out, not_4_out, main_1_p3[3]);
  Multiplexer #(.enable("false")) multiplexer_1 (.in0(and_1_out), .in1(and_2_out), .out(multiplexer_1_out), .sel(in_1));
  Hex_Digit_Display hex_digit_display_1 (.value({1'b0, counter6_1_out_3}));  // open: dp
  counter6 counter6_1 (.in_1(multiplexer_1_out), .S(in_1), .out_3(counter6_1_out_3));
  Hex_Digit_Display hex_digit_display_2 (.value(main_1_p3));  // open: dp
endmodule
