// Logisim project DECADE.circ as structural Verilog
module main (
  input  S,
  input  Clear
);

  wire and_1_out, and_2_out, and_3_out, and_4_out, and_5_out, and_6_out, and_7_out, and_8_out, and_9_out,
       and_10_out, and_11_out, clock_1_out, j_k_ff_1_qn, j_k_ff_2_qn, j_k_ff_3_qn, j_k_ff_4_qn,
       multiplexer_1_out, multiplexer_2_out, multiplexer_3_out, or_1_out, or_2_out, or_3_out;
  wire [3:0] j_k_ff_1_q;

  Clock clock_1 (.out(clock_1_out));
  Hex_Digit_Display hex_digit_display_1 (.value(j_k_ff_1_q));  // open: dp
  J_K_Flip_Flop j_k_ff_1 (
    .J(1'b1), .clk(clock_1_out), .K(1'b1), .Q(j_k_ff_1_q[0]), .Qn(j_k_ff_1_qn), .reset(Clear));  // open: preset, en
  and and_1 (and_1_out, j_k_ff_1_q[0], j_k_ff_4_qn);
  and and_2 (and_2_out, j_k_ff_1_q[1], j_k_ff_1_qn);
  and and_3 (and_3_out, j_k_ff_1_q[2], j_k_ff_1_qn);
  and and_4 (and_4_out, j_k_ff_1_q[3], j_k_ff_1_qn);
  Multiplexer #(.enable("false")) multiplexer_1 (.in0(and_1_out), .in1(or_1_out), .out(multiplexer_1_out), .sel(S));
  or or_1 (or_1_out, and_2_out, and_3_out, and_4_out);
  J_K_Flip_Flop j_k_ff_2 (
    .J(multiplexer_1_out), .clk(clock_1_out), .K(multiplexer_1_out), .Q(j_k_ff_1_q[1]), .Qn(j_k_ff_2_qn),
    .reset(Clear));  // open: preset, en
  and and_5 (and_5_out, j_k_ff_1_q[0], j_k_ff_1_q[1]);
  and and_6 (and_6_out, j_k_ff_2_qn, j_k_ff_1_qn);
  and and_7 (and_7_out, j_k_ff_1_q[2], and_6_out);
  and and_8 (and_8_out, and_6_out, j_k_ff_1_q[3]);
  Multiplexer #(.enable("false")) multiplexer_2 (.in0(and_5_out), .in1(or_2_out), .out(multiplexer_2_out), .sel(S));
  or or_2 (or_2_out, and_7_out, and_8_out);
  J_K_Flip_Flop j_k_ff_3 (
    .J(multiplexer_2_out), .clk(clock_1_out), .K(multiplexer_2_out), .Q(j_k_ff_1_q[2]), .Qn(j_k_ff_3_qn),
    .reset(Clear));  // open: preset, en
  and and_9 (and_9_out, and_5_out, j_k_ff_1_q[2]);
  and and_10 (and_10_out, j_k_ff_1_q[0], j_k_ff_1_q[3]);
  or or_3 (or_3_out, and_9_out, and_10_out);
  Multiplexer #(.enable("false")) multiplexer_3 (.in0(or_3_out), .in1(and_11_out), .out(multiplexer_3_out), .sel(S));
  and and_11 (and_11_out, j_k_ff_3_qn, j_k_ff_2_qn, j_k_ff_1_qn);
  J_K_Flip_Flop j_k_ff_4 (
    .J(multiplexer_3_out), .clk(clock_1_out), .K(multiplexer_3_out), .Q(j_k_ff_1_q[3]), .Qn(j_k_ff_4_qn),
    .reset(Clear));  // open: preset, en

  // Notes on the sheet:
  //   Clock
  //   UP(0) /DOWN(1)
endmodule

module casecade (
  input  in_1
);

  wire and_1_out, and_2_out, clock_1_out, multiplexer_1_out, not_1_out, not_2_out, not_3_out, not_4_out,
       not_5_out, not_6_out, undriven_2;
  wire [3:0] undriven;

  Clock clock_1 (.out(clock_1_out));
  main main_1 (.S(clock_1_out), .Clear(in_1));
  not not_1 (not_1_out, undriven[1]);
  not not_2 (not_2_out, undriven[3]);
  not not_3 (not_3_out, undriven[0]);
  not not_4 (not_4_out, undriven[2]);
  not not_5 (not_5_out, undriven[1]);
  not not_6 (not_6_out, undriven[2]);
  and and_1 (and_1_out, not_3_out, not_1_out, not_4_out, not_2_out);
  and and_2 (and_2_out, undriven[0], not_5_out, not_6_out, undriven[3]);
  Multiplexer #(.enable("false")) multiplexer_1 (.in0(and_1_out), .in1(and_2_out), .out(multiplexer_1_out), .sel(in_1));
  main main_2 (.S(multiplexer_1_out), .Clear(in_1));
  Hex_Digit_Display hex_digit_display_1 (.dp(undriven_2));  // open: value
  Hex_Digit_Display hex_digit_display_2 (.value(undriven));  // open: dp
endmodule
