// Logisim project HHMMSS.circ as structural Verilog: 6 circuits, main circuit main
module main (
  input  in_1,
  input  Clear,
  input  [3:0] in_3,
  input  in_4,
  output [3:0] out_5
);

  wire and_1_out, and_2_out, and_3_out, and_4_out, j_k_ff_4_qn, or_1_out;
  wire [3:0] multiplexer_1_out;

  Multiplexer #(.width(4), .enable("false")) multiplexer_1 (
    .in1(in_3), .out(multiplexer_1_out), .sel(in_4));  // open: in0
  and and_1 (and_1_out, out_5[0], j_k_ff_4_qn);
  J_K_Flip_Flop j_k_ff_1 (
    .J(1'b1), .clk(in_1), .K(1'b1), .Q(out_5[0]), .preset(multiplexer_1_out[0]), .reset(Clear));  // open: Qn, en
  J_K_Flip_Flop j_k_ff_2 (
    .J(and_1_out), .clk(in_1), .K(and_1_out), .Q(out_5[1]), .preset(multiplexer_1_out[1]), .reset(Clear));  // open: Qn, en
  and and_2 (and_2_out, out_5[0], out_5[1]);
  J_K_Flip_Flop j_k_ff_3 (
    .J(and_2_out), .clk(in_1), .K(and_2_out), .Q(out_5[2]), .preset(multiplexer_1_out[2]), .reset(Clear));  // open: Qn, en
  and and_3 (and_3_out, and_2_out, out_5[2]);
  or or_1 (or_1_out, and_3_out, and_4_out);
  and and_4 (and_4_out, out_5[0], out_5[3]);
  J_K_Flip_Flop j_k_ff_4 (
    .J(or_1_out), .clk(in_1), .K(or_1_out), .Q(out_5[3]), .Qn(j_k_ff_4_qn), .preset(multiplexer_1_out[3]),
    .reset(Clear));  // open: en
endmodule

module counter6 (
  input  in_1,
  input  Clear,
  input  [2:0] in_3,
  input  in_4,
  output [2:0] out_5
);

  wire and_1_out, and_2_out, and_3_out, j_k_ff_3_qn, or_1_out;
  wire [2:0] multiplexer_1_out;

  Multiplexer #(.width(3), .enable("false")) multiplexer_1 (
    .in1(in_3), .out(multiplexer_1_out), .sel(in_4));  // open: in0
  J_K_Flip_Flop j_k_ff_1 (
    .J(1'b1), .clk(in_1), .K(1'b1), .Q(out_5[0]), .preset(multiplexer_1_out[0]), .reset(Clear));  // open: Qn, en
  and and_1 (and_1_out, j_k_ff_3_qn, out_5[0]);
  J_K_Flip_Flop j_k_ff_2 (
    .J(and_1_out), .clk(in_1), .K(and_1_out), .Q(out_5[1]), .preset(multiplexer_1_out[1]), .reset(Clear));  // open: Qn, en
  and and_2 (and_2_out, out_5[2], out_5[0]);
  and and_3 (and_3_out, out_5[0], out_5[1]);
  or or_1 (or_1_out, and_2_out, and_3_out);
  J_K_Flip_Flop j_k_ff_3 (
    .J(or_1_out), .clk(in_1), .K(or_1_out), .Q(out_5[2]), .Qn(j_k_ff_3_qn), .preset(multiplexer_1_out[2]),
    .reset(Clear));  // open: en
endmodule

module s (
  input  in_1,
  input  in_2,
  input  [3:0] in_3,
  input  [2:0] in_4,
  input  in_5,
  output [3:0] Z,
  output [3:0] T
);

  wire and_1_out, not_1_out, not_2_out, not_3_out, not_4_out;

  main main_1 (.in_1(in_1), .Clear(in_2), .in_3(in_3), .in_4(in_5), .out_5(Z));
  not not_1 (not_1_out, Z[1]);
  not not_2 (not_2_out, Z[2]);
  not not_3 (not_3_out, Z[0]);
  not not_4 (not_4_out, Z[3]);
  and and_1 (and_1_out, not_3_out, not_1_out, not_2_out, not_4_out);
  counter6 counter6_1 (.in_1(and_1_out), .Clear(in_2), .in_3(in_4), .in_4(in_5), .out_5(T[2:0]));

  assign T[3] = 1'b0;
endmodule

module counter24 (
  input  in_1,
  input  Clear,
  input  [4:0] in_3,
  input  in_4,
  output [4:0] out_5
);

  wire and_1_out, and_2_out, and_3_out, j_k_ff_5_qn, xor_1_out;
  wire [4:0] multiplexer_1_out;

  Multiplexer #(.width(5), .enable("false")) multiplexer_1 (
    .in1(in_3), .out(multiplexer_1_out), .sel(in_4));  // open: in0
  J_K_Flip_Flop j_k_ff_1 (
    .J(1'b1), .clk(in_1), .K(1'b1), .Q(out_5[0]), .preset(multiplexer_1_out[0]), .reset(Clear));  // open: Qn, en
  and and_1 (and_1_out, out_5[0], out_5[1]);
  J_K_Flip_Flop j_k_ff_2 (
    .J(out_5[0]), .clk(in_1), .K(out_5[0]), .Q(out_5[1]), .preset(multiplexer_1_out[1]), .reset(Clear));  // open: Qn, en
  J_K_Flip_Flop j_k_ff_3 (
    .J(and_1_out), .clk(in_1), .K(and_1_out), .Q(out_5[2]), .preset(multiplexer_1_out[2]), .reset(Clear));  // open: Qn, en
  and and_2 (and_2_out, and_1_out, j_k_ff_5_qn, out_5[2]);
  J_K_Flip_Flop j_k_ff_4 (
    .J(and_2_out), .clk(in_1), .K(and_2_out), .Q(out_5[3]), .preset(multiplexer_1_out[3]), .reset(Clear));  // open: Qn, en
  and and_3 (and_3_out, and_1_out, out_5[2], xor_1_out);
  xor xor_1 (xor_1_out, out_5[3], out_5[4]);
  J_K_Flip_Flop j_k_ff_5 (
    .J(and_3_out), .clk(in_1), .K(and_3_out), .Q(out_5[4]), .Qn(j_k_ff_5_qn), .preset(multiplexer_1_out[4]),
    .reset(Clear));  // open: en
endmodule

module HHMMSS (
  input  [3:0] Ones,
  input  [3:0] Ones_2,
  input  [4:0] Hour,
  input  [2:0] Tens,
  input  [2:0] Tens_2,
  output [4:0] HOUR_2
);

  wire and_1_out, and_2_out, Clear_out, clock_1_out, Load_out, not_1_out, not_2_out, not_3_out, not_4_out,
       not_5_out, not_6_out, not_7_out, not_8_out;
  wire [3:0] MM_t, MM_z, SS_t, SS_z;

  Clock clock_1 (.out(clock_1_out));
  Button Clear (.out(Clear_out));
  Button Load (.out(Load_out));
  s SS (.in_1(clock_1_out), .in_2(Clear_out), .in_3(Ones), .in_4(Tens), .in_5(Load_out), .Z(SS_z), .T(SS_t));
  not not_1 (not_1_out, SS_t[1]);
  not not_2 (not_2_out, SS_t[2]);
  not not_3 (not_3_out, SS_t[0]);
  and and_1 (and_1_out, not_3_out, not_1_out, not_2_out, not_4_out);
  not not_4 (not_4_out, SS_t[3]);
  Hex_Digit_Display hex_digit_display_1 ();  // open: value, dp
  s MM (.in_1(and_1_out), .in_2(Clear_out), .in_3(Ones_2), .in_4(Tens_2), .in_5(Load_out), .Z(MM_z), .T(MM_t));
  Hex_Digit_Display hex_digit_display_2 (.value(MM_t));  // open: dp
  Hex_Digit_Display hex_digit_display_3 (.value(MM_z));  // open: dp
  Hex_Digit_Display hex_digit_display_4 ();  // open: value, dp
  not not_5 (not_5_out, MM_t[0]);
  not not_6 (not_6_out, MM_t[1]);
  not not_7 (not_7_out, MM_t[2]);
  not not_8 (not_8_out, MM_t[3]);
  Hex_Digit_Display hex_digit_display_5 (.value(SS_t));  // open: dp
  Hex_Digit_Display hex_digit_display_6 (.value(SS_z));  // open: dp
  and and_2 (and_2_out, not_5_out, not_6_out, not_7_out, not_8_out);
  counter24 HH (.in_1(and_2_out), .Clear(Clear_out), .in_3(Hour), .in_4(Load_out), .out_5(HOUR_2));

  // Notes on the sheet:
  //   MINUTES
  //   SECONDS
endmodule

module mod2 (
);

  wire j_k_ff_2_qn, undriven, undriven_3;
  wire [1:0] j_k_ff_1_q;
  wire [3:0] undriven_2;

  J_K_Flip_Flop j_k_ff_1 (.J(j_k_ff_2_qn), .clk(undriven), .K(1'b1), .Q(j_k_ff_1_q[0]));  // open: Qn, preset, en, reset
  J_K_Flip_Flop j_k_ff_2 (
    .J(j_k_ff_1_q[0]), .clk(undriven), .K(1'b1), .Q(j_k_ff_1_q[1]), .Qn(j_k_ff_2_qn));  // open: preset, en, reset
  Hex_Digit_Display hex_digit_display_1 (.value(undriven_2), .dp(undriven_3));
endmodule
