// Logisim project MINUTE (1).circ as structural Verilog: 6 circuits, main circuit main
module main (
  input  in_1,
  input  S,
  input  Clear,
  output [3:0] out_4
);

  wire and_1_out, and_2_out, and_3_out, and_4_out, and_5_out, and_6_out, and_7_out, and_8_out, and_9_out,
       and_10_out, and_11_out, j_k_ff_1_qn, j_k_ff_2_qn, j_k_ff_3_qn, j_k_ff_4_qn, multiplexer_1_out,
       multiplexer_2_out, multiplexer_3_out, or_1_out, or_2_out, or_3_out;

  J_K_Flip_Flop j_k_ff_1 (
    .J(1'b1), .clk(in_1), .K(1'b1), .Q(out_4[0]), .Qn(j_k_ff_1_qn), .reset(Clear));  // open: preset, en
  and and_1 (and_1_out, out_4[0], j_k_ff_4_qn);
  and and_2 (and_2_out, out_4[1], j_k_ff_1_qn);
  and and_3 (and_3_out, out_4[2], j_k_ff_1_qn);
  and and_4 (and_4_out, out_4[3], j_k_ff_1_qn);
  Multiplexer #(.enable("false")) multiplexer_1 (.in0(and_1_out), .in1(or_1_out), .out(multiplexer_1_out), .sel(S));
  or or_1 (or_1_out, and_2_out, and_3_out, and_4_out);
  J_K_Flip_Flop j_k_ff_2 (
    .J(multiplexer_1_out), .clk(in_1), .K(multiplexer_1_out), .Q(out_4[1]), .Qn(j_k_ff_2_qn), .reset(Clear));  // open: preset, en
  and and_5 (and_5_out, out_4[0], out_4[1]);
  and and_6 (and_6_out, j_k_ff_2_qn, j_k_ff_1_qn);
  and and_7 (and_7_out, out_4[2], and_6_out);
  and and_8 (and_8_out, and_6_out, out_4[3]);
  Multiplexer #(.enable("false")) multiplexer_2 (.in0(and_5_out), .in1(or_2_out), .out(multiplexer_2_out), .sel(S));
  or or_2 (or_2_out, and_7_out, and_8_out);
  J_K_Flip_Flop j_k_ff_3 (
    .J(multiplexer_2_out), .clk(in_1), .K(multiplexer_2_out), .Q(out_4[2]), .Qn(j_k_ff_3_qn), .reset(Clear));  // open: preset, en
  and and_9 (and_9_out, and_5_out, out_4[2]);
  or or_3 (or_3_out, and_9_out, and_10_out);
  and and_10 (and_10_out, out_4[0], out_4[3]);
  and and_11 (and_11_out, j_k_ff_3_qn, j_k_ff_2_qn, j_k_ff_1_qn);
  Multiplexer #(.enable("false")) multiplexer_3 (.in0(or_3_out), .in1(and_11_out), .out(multiplexer_3_out), .sel(S));
  J_K_Flip_Flop j_k_ff_4 (
    .J(multiplexer_3_out), .clk(in_1), .K(multiplexer_3_out), .Q(out_4[3]), .Qn(j_k_ff_4_qn), .reset(Clear));  // open: preset, en

  // Notes on the sheet:
  //   Mod 10 counter
endmodule

module counter6 (
  input  in_1,
  input  S,
  input  Clear,
  output [2:0] out_4
);

  wire and_1_out, and_2_out, and_3_out, and_4_out, and_5_out, and_6_out, j_k_ff_1_qn, j_k_ff_2_qn,
       j_k_ff_3_qn, multiplexer_1_out, multiplexer_2_out, or_1_out, or_2_out;

  J_K_Flip_Flop j_k_ff_1 (
    .J(1'b1), .clk(in_1), .K(1'b1), .Q(out_4[0]), .Qn(j_k_ff_1_qn), .reset(Clear));  // open: preset, en
  and and_1 (and_1_out, j_k_ff_3_qn, out_4[0]);
  and and_2 (and_2_out, out_4[2], j_k_ff_1_qn);
  or or_1 (or_1_out, and_2_out, and_3_out);
  and and_3 (and_3_out, j_k_ff_1_qn, out_4[1]);
  Multiplexer #(.enable("false")) multiplexer_1 (.in0(and_1_out), .in1(or_1_out), .out(multiplexer_1_out), .sel(S));
  J_K_Flip_Flop j_k_ff_2 (
    .J(multiplexer_1_out), .clk(in_1), .K(multiplexer_1_out), .Q(out_4[1]), .Qn(j_k_ff_2_qn), .reset(Clear));  // open: preset, en
  and and_4 (and_4_out, out_4[2], out_4[0]);
  or or_2 (or_2_out, and_4_out, and_5_out);
  and and_5 (and_5_out, out_4[0], out_4[1]);
  and and_6 (and_6_out, j_k_ff_2_qn, j_k_ff_1_qn);
  Multiplexer #(.enable("false")) multiplexer_2 (.in0(or_2_out), .in1(and_6_out), .out(multiplexer_2_out), .sel(S));
  J_K_Flip_Flop j_k_ff_3 (
    .J(multiplexer_2_out), .clk(in_1), .K(multiplexer_2_out), .Q(out_4[2]), .Qn(j_k_ff_3_qn), .reset(Clear));  // open: preset, en

  // Notes on the sheet:
  //   Mod 6 counter
endmodule

module minute (
  input  in_1
);

  wire and_1_out, and_2_out, button_1_out, clock_1_out, multiplexer_1_out, not_1_out, not_2_out, not_3_out,
       not_4_out, not_5_out, not_6_out;
  wire [2:0] counter6_1_out_4;
  wire [3:0] main_1_out_4;

  Clock clock_1 (.out(clock_1_out));
  main main_1 (.in_1(clock_1_out), .S(in_1), .Clear(button_1_out), .out_4(main_1_out_4));
  Button button_1 (.out(button_1_out));
  not not_1 (not_1_out, main_1_out_4[1]);
  not not_2 (not_2_out, main_1_out_4[2]);
  not not_3 (not_3_out, main_1_out_4[1]);
  not not_4 (not_4_out, main_1_out_4[2]);
  not not_5 (not_5_out, main_1_out_4[0]);
  not not_6 (not_6_out, main_1_out_4[3]);
  and and_1 (and_1_out, not_5_out, not_1_out, not_2_out, not_6_out);
  and and_2 (and_2_out, main_1_out_4[0], not_3_out, not_4_out, main_1_out_4[3]);
  Multiplexer #(.enable("false")) multiplexer_1 (.in0(and_1_out), .in1(and_2_out), .out(multiplexer_1_out), .sel(in_1));
  Hex_Digit_Display hex_digit_display_1 (.value({1'b0, counter6_1_out_4}));  // open: dp
  counter6 counter6_1 (.in_1(multiplexer_1_out), .S(in_1), .Clear(button_1_out), .out_4(counter6_1_out_4));
  Hex_Digit_Display hex_digit_display_2 (.value(main_1_out_4));  // open: dp

  // Notes on the sheet:
  //   Mod 60 counter
endmodule

module HHMMSS (
  input  in_1,
  output [4:0] out_2
);

  wire and_1_out, and_2_out, and_3_out, and_4_out, Clear_out, clock_1_out, multiplexer_1_out,
       multiplexer_2_out, not_1_out, not_2_out, not_3_out, not_4_out, not_5_out, not_6_out, not_7_out,
       not_8_out, not_9_out, not_10_out, not_11_out, not_12_out;
  wire [3:0] MM_t, MM_z, SS_t, SS_z;

  Clock clock_1 (.out(clock_1_out));
  Button Clear (.out(Clear_out));
  s SS (.in_1(clock_1_out), .in_2(in_1), .in_3(Clear_out), .Z(SS_z), .T(SS_t));
  not not_1 (not_1_out, SS_t[0]);
  not not_2 (not_2_out, SS_t[1]);
  not not_3 (not_3_out, SS_t[2]);
  not not_4 (not_4_out, SS_t[3]);
  not not_5 (not_5_out, SS_t[1]);
  not not_6 (not_6_out, SS_t[3]);
  Multiplexer #(.enable("false")) multiplexer_1 (.in0(and_1_out), .in1(and_2_out), .out(multiplexer_1_out), .sel(in_1));
  and and_1 (and_1_out, not_1_out, not_2_out, not_3_out, not_4_out);
  and and_2 (and_2_out, SS_t[0], not_5_out, SS_t[2], not_6_out);
  Hex_Digit_Display hex_digit_display_1 ();  // open: value, dp
  s MM (.in_1(multiplexer_1_out), .in_2(in_1), .in_3(Clear_out), .Z(MM_z), .T(MM_t));
  Hex_Digit_Display hex_digit_display_2 (.value(MM_t));  // open: dp
  Hex_Digit_Display hex_digit_display_3 (.value(MM_z));  // open: dp
  Hex_Digit_Display hex_digit_display_4 ();  // open: value, dp
  not not_7 (not_7_out, MM_t[1]);
  not not_8 (not_8_out, MM_t[2]);
  not not_9 (not_9_out, MM_t[1]);
  not not_10 (not_10_out, MM_t[3]);
  Hex_Digit_Display hex_digit_display_5 (.value(SS_t));  // open: dp
  Hex_Digit_Display hex_digit_display_6 (.value(SS_z));  // open: dp
  not not_11 (not_11_out, MM_t[0]);
  not not_12 (not_12_out, MM_t[3]);
  and and_3 (and_3_out, not_11_out, not_7_out, not_8_out, not_12_out);
  and and_4 (and_4_out, MM_t[0], not_9_out, MM_t[2], not_10_out);
  Multiplexer #(.enable("false")) multiplexer_2 (.in0(and_3_out), .in1(and_4_out), .out(multiplexer_2_out), .sel(in_1));
  counter24 HH (.in_1(multiplexer_2_out), .S(in_1), .Clear(Clear_out), .out_4(out_2));
endmodule

module s (
  input  in_1,
  input  in_2,
  input  in_3,
  output [3:0] Z,
  output [3:0] T
);

  wire and_1_out, and_2_out, multiplexer_1_out, not_1_out, not_2_out, not_3_out, not_4_out, not_5_out,
       not_6_out;

  main main_1 (.in_1(in_1), .S(in_2), .Clear(in_3), .out_4(Z));
  not not_1 (not_1_out, Z[1]);
  not not_2 (not_2_out, Z[2]);
  not not_3 (not_3_out, Z[1]);
  not not_4 (not_4_out, Z[2]);
  not not_5 (not_5_out, Z[0]);
  not not_6 (not_6_out, Z[3]);
  and and_1 (and_1_out, not_5_out, not_1_out, not_2_out, not_6_out);
  Multiplexer #(.enable("false")) multiplexer_1 (.in0(and_1_out), .in1(and_2_out), .out(multiplexer_1_out), .sel(in_2));
  and and_2 (and_2_out, Z[0], not_3_out, not_4_out, Z[3]);
  counter6 counter6_1 (.in_1(multiplexer_1_out), .S(in_2), .Clear(in_3), .out_4(T[2:0]));

  assign T[3] = 1'b0;
endmodule

module counter24 (
  input  in_1,
  input  S,
  input  Clear,
  output [4:0] out_4
);

  wire and_1_out, and_2_out, and_3_out, and_4_out, and_5_out, and_6_out, j_k_ff_1_qn, j_k_ff_2_qn,
       j_k_ff_3_qn, j_k_ff_4_qn, j_k_ff_5_qn, multiplexer_1_out, multiplexer_2_out, multiplexer_3_out,
       multiplexer_4_out, xor_1_out;

  J_K_Flip_Flop j_k_ff_1 (
    .J(1'b1), .clk(in_1), .K(1'b1), .Q(out_4[0]), .Qn(j_k_ff_1_qn), .reset(Clear));  // open: preset, en
  Multiplexer #(.enable("false")) multiplexer_1 (.in0(out_4[0]), .in1(j_k_ff_1_qn), .out(multiplexer_1_out), .sel(S));
  and and_1 (and_1_out, out_4[0], out_4[1]);
  J_K_Flip_Flop j_k_ff_2 (
    .J(multiplexer_1_out), .clk(in_1), .K(multiplexer_1_out), .Q(out_4[1]), .Qn(j_k_ff_2_qn), .reset(Clear));  // open: preset, en
  and and_2 (and_2_out, j_k_ff_2_qn, j_k_ff_1_qn);
  Multiplexer #(.enable("false")) multiplexer_2 (.in0(and_1_out), .in1(and_2_out), .out(multiplexer_2_out), .sel(S));
  J_K_Flip_Flop j_k_ff_3 (
    .J(multiplexer_2_out), .clk(in_1), .K(multiplexer_2_out), .Q(out_4[2]), .Qn(j_k_ff_3_qn), .reset(Clear));  // open: preset, en
  xor xor_1 (xor_1_out, out_4[3], out_4[4]);
  and and_3 (and_3_out, and_1_out, j_k_ff_5_qn, out_4[2]);
  and and_4 (and_4_out, j_k_ff_3_qn, and_2_out, xor_1_out);
  Multiplexer #(.enable("false")) multiplexer_3 (.in0(and_3_out), .in1(and_4_out), .out(multiplexer_3_out), .sel(S));
  J_K_Flip_Flop j_k_ff_4 (
    .J(multiplexer_3_out), .clk(in_1), .K(multiplexer_3_out), .Q(out_4[3]), .Qn(j_k_ff_4_qn), .reset(Clear));  // open: preset, en
  and and_5 (and_5_out, and_1_out, out_4[2], xor_1_out);
  and and_6 (and_6_out, j_k_ff_4_qn, j_k_ff_3_qn, and_2_out);
  Multiplexer #(.enable("false")) multiplexer_4 (.in0(and_5_out), .in1(and_6_out), .out(multiplexer_4_out), .sel(S));
  J_K_Flip_Flop j_k_ff_5 (
    .J(multiplexer_4_out), .clk(in_1), .K(multiplexer_4_out), .Q(out_4[4]), .Qn(j_k_ff_5_qn), .reset(Clear));  // open: preset, en
endmodule
