// Logisim project Traffic.circ as structural Verilog: 12 circuits, main circuit main
module main (
  input  [3:0] in_1,
  input  [3:0] in_2,
  input  [3:0] in_3,
  input  [3:0] in_4,
  input  [3:0] in_5,
  input  [3:0] in_6
);

  wire CLEAR_out, CLOCK_out, SET_out;
  wire [3:0] n24_hr_clock_1_hr_0, n24_hr_clock_1_hr_1, n24_hr_clock_1_min_0, n24_hr_clock_1_min_1,
       n24_hr_clock_1_sec_0, n24_hr_clock_1_sec_1, signal_1_higher_4_bit, signal_1_lower_4_bit,
       signal_1_out_5, signal_1_out_8, signal_1_out_9, signal_1_out_10;

  Hex_Digit_Display hex_digit_display_1 (.value(signal_1_higher_4_bit));  // open: dp
  Hex_Digit_Display hex_digit_display_2 (.value(signal_1_lower_4_bit));  // open: dp
  LED L (.in(signal_1_out_9[0]));
  LED led_1 (.in(signal_1_out_9[1]));
  LED S (.in(signal_1_out_9[2]));
  LED R (.in(signal_1_out_9[3]));
  LED L_2 (.in(signal_1_out_10[3]));
  signal signal_1 (
    .out_9(signal_1_out_9), .HIGHER_4_BIT(signal_1_higher_4_bit), .INPUT_1(n24_hr_clock_1_hr_1),
    .LOWER_4_BIT(signal_1_lower_4_bit), .INPUT_0(n24_hr_clock_1_hr_0), .out_5(signal_1_out_5),
    .CLOCK(CLOCK_out), .out_10(signal_1_out_10), .out_8(signal_1_out_8), .CLEAR(CLEAR_out));
  LED led_2 (.in(signal_1_out_10[2]));
  LED S_2 (.in(signal_1_out_10[1]));
  LED R_2 (.in(signal_1_out_10[0]));
  LED led_3 (.in(signal_1_out_5[1]));
  LED S_3 (.in(signal_1_out_5[2]));
  LED L_3 (.in(signal_1_out_5[0]));
  LED R_3 (.in(signal_1_out_5[3]));
  LED R_4 (.in(signal_1_out_8[0]));
  LED S_4 (.in(signal_1_out_8[1]));
  LED led_4 (.in(signal_1_out_8[2]));
  LED L_4 (.in(signal_1_out_8[3]));
  Hex_Digit_Display hex_digit_display_3 (.value(n24_hr_clock_1_hr_0));  // open: dp
  Hex_Digit_Display hex_digit_display_4 (.value(n24_hr_clock_1_hr_1));  // open: dp
  LED led_5 ();  // open: in
  LED led_6 ();  // open: in
  Hex_Digit_Display hex_digit_display_5 (.value(n24_hr_clock_1_min_1));  // open: dp
  LED led_7 ();  // open: in
  LED led_8 ();  // open: in
  Hex_Digit_Display hex_digit_display_6 (.value(n24_hr_clock_1_min_0));  // open: dp
  Clock CLOCK (.out(CLOCK_out));
  Button CLEAR (.out(CLEAR_out));
  Hex_Digit_Display hex_digit_display_7 (.value(n24_hr_clock_1_sec_1));  // open: dp
  Button SET (.out(SET_out));
  Hex_Digit_Display hex_digit_display_8 (.value(n24_hr_clock_1_sec_0));  // open: dp
  _24_HR_CLOCK u_24_hr_clock_1 (
    .HR_1(n24_hr_clock_1_hr_1), .HR_0(n24_hr_clock_1_hr_0), .MIN_1(n24_hr_clock_1_min_1),
    .SEC_1(n24_hr_clock_1_sec_1), .MIN_0(n24_hr_clock_1_min_0), .SEC_0(n24_hr_clock_1_sec_0),
    .CLEAR(CLEAR_out), .CLOCK(CLOCK_out), .HR_1_INPUT(in_1), .HR_0_INPUT(in_2), .MIN_1_INPUT(in_5),
    .MIN_0_INPUT(in_6), .SEC_1_INPUT(in_3), .SEC_0_INPUT(in_4), .SET(SET_out));
endmodule

module signal (
  input  CLOCK,
  input  [3:0] INPUT_1,
  input  [3:0] INPUT_0,
  input  CLEAR,
  output [3:0] out_5,
  output [3:0] HIGHER_4_BIT,
  output [3:0] LOWER_4_BIT,
  output [3:0] out_8,
  output [3:0] out_9,
  output [3:0] out_10
);

  wire and_1_out, demultiplexer_1_out0, demultiplexer_1_out1, not_1_out, not_2_out, not_3_out, not_4_out,
       not_5_out, not_7_out, not_10_out, not_11_out, not_12_out, time_selector_1_output;
  wire [3:0] MOD_4_output, MOD_30_ones, MOD_30_tens, MOD_60_ones, MOD_60_tens;

  Demultiplexer #(.enable("false")) demultiplexer_1 (
    .out0(demultiplexer_1_out0), .out1(demultiplexer_1_out1), .in(CLOCK), .sel(not_1_out));
  Hex_Digit_Display hex_digit_display_1 (.value(HIGHER_4_BIT));  // open: dp
  Multiplexer #(.width(4), .enable("false")) multiplexer_1 (
    .in0(MOD_60_tens), .in1(MOD_30_tens), .out(HIGHER_4_BIT), .sel(not_1_out));
  Hex_Digit_Display hex_digit_display_2 (.value(LOWER_4_BIT));  // open: dp
  Multiplexer #(.width(4), .enable("false")) multiplexer_2 (
    .in0(MOD_60_ones), .in1(MOD_30_ones), .out(LOWER_4_BIT), .sel(not_1_out));
  MOD_60_UP_COUNTER MOD_60 (
    .CLOCK(demultiplexer_1_out0), .CLEAR(CLEAR), .TENS(MOD_60_tens), .ONES(MOD_60_ones));  // open: USER_INPUT_1, USER_INPUT_0, SWITCH
  MOD_30_UP_COUNTER MOD_30 (
    .CLOCK(demultiplexer_1_out1), .CLEAR(CLEAR), .TENS(MOD_30_tens), .ONES(MOD_30_ones));  // open: USER_INPUT_1, USER_INPUT_0, SWITCH
  not not_1 (not_1_out, time_selector_1_output);
  not not_2 (not_2_out, HIGHER_4_BIT[0]);
  not not_3 (not_3_out, HIGHER_4_BIT[1]);
  not not_4 (not_4_out, HIGHER_4_BIT[2]);
  not not_5 (not_5_out, HIGHER_4_BIT[3]);
  TIME_SELECTOR time_selector_1 (.INPUT_1(INPUT_1), .INPUT_0(INPUT_0), .OUTPUT(time_selector_1_output));
  and and_1 (and_1_out, not_2_out, not_3_out, not_4_out, not_5_out);
  MOD_4 MOD_4 (.CLOCK(and_1_out), .OUTPUT({{2{MOD_4_output[3]}}, MOD_4_output[1:0]}));  // open: CLEAR
  Hex_Digit_Display hex_digit_display_3 (.value({{2{MOD_4_output[3]}}, MOD_4_output[1:0]}));  // open: dp
  not not_6 (out_9[1], out_9[3]);
  and and_2 (out_9[3], MOD_4_output[1], MOD_4_output[0]);
  not not_7 (not_7_out, MOD_4_output[0]);
  and and_3 (out_10[1], MOD_4_output[1], not_7_out);
  not not_8 (out_10[2], out_10[1]);
  not not_9 (out_5[1], out_5[3]);
  and and_4 (out_5[3], not_10_out, not_11_out);
  not not_10 (not_10_out, MOD_4_output[0]);
  not not_11 (not_11_out, MOD_4_output[1]);
  not not_12 (not_12_out, MOD_4_output[1]);
  and and_5 (out_8[1], not_12_out, MOD_4_output[0]);
  not not_13 (out_8[2], out_8[1]);

  assign {out_5[2], out_5[0]} = {out_5[3], 1'b1};
  assign {out_8[3], out_8[0]} = {1'b1, out_8[1]};
  assign {out_9[2], out_9[0]} = {out_9[3], 1'b1};
  assign {out_10[3], out_10[0]} = {1'b1, out_10[1]};
  // also tied to GND on the sheet: MOD_4_output[3]
endmodule

module decade_counter (
  input  [3:0] USER_INPUT,
  input  SWITCH,
  input  CLOCK,
  input  CLEAR,
  output [3:0] OUTPUT
);

  wire and_1_out, and_2_out, and_3_out, and_4_out, and_5_out, and_6_out, and_7_out, j_k_ff_1_qn, j_k_ff_2_qn,
       j_k_ff_3_qn, j_k_ff_4_qn, multiplexer_1_out, multiplexer_2_out, multiplexer_3_out, multiplexer_4_out,
       multiplexer_5_out, multiplexer_6_out, not_1_out, or_1_out, or_2_out, or_3_out, or_4_out, or_5_out,
       PARALLEL_LOADING_clear_0, PARALLEL_LOADING_clear_1, PARALLEL_LOADING_clear_2,
       PARALLEL_LOADING_clear_3, PARALLEL_LOADING_preset_0, PARALLEL_LOADING_preset_1,
       PARALLEL_LOADING_preset_2, PARALLEL_LOADING_preset_3;

  Hex_Digit_Display hex_digit_display_1 (.value(USER_INPUT));  // open: dp
  value_set PARALLEL_LOADING (
    .USER_INPUT(USER_INPUT), .SWITCH(SWITCH), .PRESET_3(PARALLEL_LOADING_preset_3),
    .CLEAR_3(PARALLEL_LOADING_clear_3), .PRESET_2(PARALLEL_LOADING_preset_2),
    .CLEAR_2(PARALLEL_LOADING_clear_2), .PRESET_1(PARALLEL_LOADING_preset_1),
    .CLEAR_1(PARALLEL_LOADING_clear_1), .PRESET_0(PARALLEL_LOADING_preset_0),
    .CLEAR_0(PARALLEL_LOADING_clear_0));
  not not_1 (not_1_out, 1'b1);
  Multiplexer #(.enable("false")) multiplexer_1 (
    .in0(and_1_out), .in1(and_2_out), .out(multiplexer_1_out), .sel(not_1_out));
  Multiplexer #(.enable("false")) multiplexer_2 (
    .in0(OUTPUT[0]), .in1(j_k_ff_4_qn), .out(multiplexer_2_out), .sel(not_1_out));
  J_K_Flip_Flop j_k_ff_1 (
    .J(multiplexer_1_out), .clk(CLOCK), .K(multiplexer_2_out), .Q(OUTPUT[3]), .Qn(j_k_ff_1_qn),
    .preset(PARALLEL_LOADING_preset_3), .en(1'b1), .reset(or_1_out));
  or or_1 (or_1_out, PARALLEL_LOADING_clear_3, CLEAR);
  and and_1 (and_1_out, and_4_out, OUTPUT[2]);
  and and_2 (and_2_out, j_k_ff_2_qn, and_5_out);
  or or_2 (or_2_out, OUTPUT[2], OUTPUT[3]);
  Multiplexer #(.enable("false")) multiplexer_3 (
    .in0(and_4_out), .in1(and_3_out), .out(multiplexer_3_out), .sel(not_1_out));
  Multiplexer #(.enable("false")) multiplexer_4 (
    .in0(and_4_out), .in1(and_5_out), .out(multiplexer_4_out), .sel(not_1_out));
  J_K_Flip_Flop j_k_ff_2 (
    .J(multiplexer_3_out), .clk(CLOCK), .K(multiplexer_4_out), .Q(OUTPUT[2]), .Qn(j_k_ff_2_qn),
    .preset(PARALLEL_LOADING_preset_2), .en(1'b1), .reset(or_3_out));
  and and_3 (and_3_out, OUTPUT[3], j_k_ff_4_qn);
  and and_4 (and_4_out, OUTPUT[0], OUTPUT[1]);
  and and_5 (and_5_out, j_k_ff_4_qn, j_k_ff_3_qn);
  or or_3 (or_3_out, PARALLEL_LOADING_clear_2, CLEAR);
  Multiplexer #(.enable("false")) multiplexer_5 (
    .in0(and_7_out), .in1(and_6_out), .out(multiplexer_5_out), .sel(not_1_out));
  Multiplexer #(.enable("false")) multiplexer_6 (
    .in0(OUTPUT[0]), .in1(j_k_ff_4_qn), .out(multiplexer_6_out), .sel(not_1_out));
  and and_6 (and_6_out, or_2_out, j_k_ff_4_qn);
  J_K_Flip_Flop j_k_ff_3 (
    .J(multiplexer_5_out), .clk(CLOCK), .K(multiplexer_6_out), .Q(OUTPUT[1]), .Qn(j_k_ff_3_qn),
    .preset(PARALLEL_LOADING_preset_1), .en(1'b1), .reset(or_4_out));
  or or_4 (or_4_out, PARALLEL_LOADING_clear_1, CLEAR);
  and and_7 (and_7_out, j_k_ff_1_qn, OUTPUT[0]);
  J_K_Flip_Flop j_k_ff_4 (
    .J(1'b1), .clk(CLOCK), .K(1'b1), .Q(OUTPUT[0]), .Qn(j_k_ff_4_qn), .preset(PARALLEL_LOADING_preset_0),
    .en(1'b1), .reset(or_5_out));
  Hex_Digit_Display hex_digit_display_2 (.value(OUTPUT));  // open: dp
  or or_5 (or_5_out, PARALLEL_LOADING_clear_0, CLEAR);

  // Notes on the sheet:
  //   UP
  //   DECADE
  //   COUNTER
  //   USING
  //   J-K  F/F
endmodule

module MOD_6_UP_COUNTER (
  input  [3:0] USER_INPUT,
  input  SWITCH,
  input  CLOCK,
  input  CLEAR,
  output [3:0] OUTPUT
);

  wire and_1_out, and_2_out, or_1_out, or_2_out, or_3_out, or_4_out, PARALLEL_LOADING_clear_0,
       PARALLEL_LOADING_clear_1, PARALLEL_LOADING_clear_2, PARALLEL_LOADING_preset_0,
       PARALLEL_LOADING_preset_1, PARALLEL_LOADING_preset_2, t_ff_1_qn;

  Hex_Digit_Display hex_digit_display_1 (.value(USER_INPUT));  // open: dp
  value_set PARALLEL_LOADING (
    .USER_INPUT(USER_INPUT), .SWITCH(SWITCH), .PRESET_2(PARALLEL_LOADING_preset_2),
    .CLEAR_2(PARALLEL_LOADING_clear_2), .PRESET_1(PARALLEL_LOADING_preset_1),
    .CLEAR_1(PARALLEL_LOADING_clear_1), .PRESET_0(PARALLEL_LOADING_preset_0),
    .CLEAR_0(PARALLEL_LOADING_clear_0));  // open: PRESET_3, CLEAR_3
  and and_1 (and_1_out, or_2_out, OUTPUT[0]);
  T_Flip_Flop t_ff_1 (
    .clk(CLOCK), .T(and_1_out), .Q(OUTPUT[2]), .Qn(t_ff_1_qn), .preset(PARALLEL_LOADING_preset_2),
    .reset(or_1_out), .en(1'b1));
  or or_1 (or_1_out, CLEAR, PARALLEL_LOADING_clear_2);
  or or_2 (or_2_out, OUTPUT[2], OUTPUT[1]);
  T_Flip_Flop t_ff_2 (
    .clk(CLOCK), .T(and_2_out), .Q(OUTPUT[1]), .preset(PARALLEL_LOADING_preset_1), .reset(or_3_out), .en(1'b1));  // open: Qn
  and and_2 (and_2_out, t_ff_1_qn, OUTPUT[0]);
  or or_3 (or_3_out, CLEAR, PARALLEL_LOADING_clear_1);
  T_Flip_Flop t_ff_3 (
    .clk(CLOCK), .T(1'b1), .Q(OUTPUT[0]), .preset(PARALLEL_LOADING_preset_0), .reset(or_4_out), .en(1'b1));  // open: Qn
  or or_4 (or_4_out, CLEAR, PARALLEL_LOADING_clear_0);
  not not_1 (OUTPUT[3], 1'b1);
  Hex_Digit_Display hex_digit_display_2 (.value(OUTPUT));  // open: dp

  // Notes on the sheet:
  //   MOD 6 UP COUNTER
endmodule

module MOD_60_UP_COUNTER (
  input  CLOCK,
  input  CLEAR,
  input  [3:0] USER_INPUT_1,
  input  [3:0] USER_INPUT_0,
  input  SWITCH,
  output [3:0] TENS,
  output [3:0] ONES
);

  wire and_1_out, not_1_out, not_2_out, not_3_out, not_4_out;

  MOD_6_UP_COUNTER MOD_6_COUNTER (
    .CLOCK(and_1_out), .CLEAR(CLEAR), .SWITCH(SWITCH), .USER_INPUT(USER_INPUT_1), .OUTPUT(TENS));
  decade_counter DECADE_COUNTER (
    .CLOCK(CLOCK), .CLEAR(CLEAR), .SWITCH(SWITCH), .USER_INPUT(USER_INPUT_0), .OUTPUT(ONES));
  not not_1 (not_1_out, ONES[3]);
  not not_2 (not_2_out, ONES[2]);
  not not_3 (not_3_out, ONES[1]);
  and and_1 (and_1_out, not_1_out, not_2_out, not_3_out, not_4_out);
  not not_4 (not_4_out, ONES[0]);
  Hex_Digit_Display hex_digit_display_1 (.value(TENS));  // open: dp
  Hex_Digit_Display hex_digit_display_2 (.value(ONES));  // open: dp
  Hex_Digit_Display hex_digit_display_3 (.value(USER_INPUT_1));  // open: dp
  Hex_Digit_Display hex_digit_display_4 (.value(USER_INPUT_0));  // open: dp

  // Notes on the sheet:
  //   MOD 60 UP COUNTER
endmodule

module MOD_4 (
  input  CLOCK,
  input  CLEAR,
  output [3:0] OUTPUT
);

  wire and_1_out, and_2_out, and_3_out, not_1_out, not_3_out, or_1_out, or_2_out, t_ff_1_qn;

  and and_1 (and_1_out, or_2_out, OUTPUT[0]);
  T_Flip_Flop t_ff_1 (
    .clk(CLOCK), .T(and_1_out), .Q(OUTPUT[2]), .Qn(t_ff_1_qn), .reset(or_1_out), .en(1'b1));  // open: preset
  or or_1 (or_1_out, CLEAR, and_3_out);
  or or_2 (or_2_out, OUTPUT[2], OUTPUT[1]);
  and and_2 (and_2_out, t_ff_1_qn, OUTPUT[0]);
  T_Flip_Flop t_ff_2 (.clk(CLOCK), .T(and_2_out), .Q(OUTPUT[1]), .reset(or_1_out), .en(1'b1));  // open: Qn, preset
  T_Flip_Flop t_ff_3 (.clk(CLOCK), .T(1'b1), .Q(OUTPUT[0]), .reset(or_1_out), .en(1'b1));  // open: Qn, preset
  not not_1 (not_1_out, OUTPUT[1]);
  and and_3 (and_3_out, OUTPUT[2], not_1_out, not_3_out);
  not not_2 (OUTPUT[3], 1'b1);
  not not_3 (not_3_out, OUTPUT[0]);
  Hex_Digit_Display hex_digit_display_1 (.value(OUTPUT));  // open: dp

  // Notes on the sheet:
  //   MOD 4 UP COUNTER
endmodule

module value_set (
  input  [3:0] USER_INPUT,
  input  SWITCH,
  output PRESET_3,
  output PRESET_2,
  output PRESET_1,
  output PRESET_0,
  output CLEAR_3,
  output CLEAR_2,
  output CLEAR_1,
  output CLEAR_0
);

  wire not_1_out, not_2_out, not_3_out, not_4_out;

  Hex_Digit_Display hex_digit_display_1 (.value(USER_INPUT));  // open: dp
  not not_1 (not_1_out, USER_INPUT[3]);
  Multiplexer #(.enable("false")) multiplexer_1 (.in0(SWITCH), .in1(USER_INPUT[3]), .out(PRESET_3), .sel(SWITCH));
  Multiplexer #(.enable("false")) multiplexer_2 (.in0(SWITCH), .in1(not_1_out), .out(CLEAR_3), .sel(SWITCH));
  not not_2 (not_2_out, USER_INPUT[2]);
  Multiplexer #(.enable("false")) multiplexer_3 (.in0(SWITCH), .in1(USER_INPUT[2]), .out(PRESET_2), .sel(SWITCH));
  Multiplexer #(.enable("false")) multiplexer_4 (.in0(SWITCH), .in1(USER_INPUT[1]), .out(PRESET_1), .sel(SWITCH));
  Multiplexer #(.enable("false")) multiplexer_5 (.in0(SWITCH), .in1(not_2_out), .out(CLEAR_2), .sel(SWITCH));
  not not_3 (not_3_out, USER_INPUT[1]);
  Multiplexer #(.enable("false")) multiplexer_6 (.in0(SWITCH), .in1(USER_INPUT[0]), .out(PRESET_0), .sel(SWITCH));
  Multiplexer #(.enable("false")) multiplexer_7 (.in0(SWITCH), .in1(not_3_out), .out(CLEAR_1), .sel(SWITCH));
  not not_4 (not_4_out, USER_INPUT[0]);
  Multiplexer #(.enable("false")) multiplexer_8 (.in0(SWITCH), .in1(not_4_out), .out(CLEAR_0), .sel(SWITCH));

  // Notes on the sheet:
  //   PARALLEL LOADING CIRCUIT
endmodule

module MOD_24_UP_COUNTER (
  input  CLOCK,
  input  [3:0] USER_INPUT_1,
  input  [3:0] USER_INPUT_0,
  input  SWITCH,
  input  CLEAR,
  output [3:0] TENS,
  output [3:0] ONES
);

  wire and_1_out, and_2_out, and_3_out, and_4_out, not_1_out, not_2_out, not_3_out, not_4_out, not_5_out,
       not_6_out, not_7_out, not_8_out, not_9_out, not_10_out, or_1_out;

  MOD_3_UP_COUNTER MOD_3_counter (
    .CLOCK(and_2_out), .CLEAR(or_1_out), .SWITCH(SWITCH), .USER_INPUT(USER_INPUT_1), .OUTPUT(TENS));
  not not_1 (not_1_out, TENS[3]);
  not not_2 (not_2_out, TENS[2]);
  and and_1 (and_1_out, not_1_out, not_2_out, TENS[1], not_3_out);
  not not_3 (not_3_out, TENS[0]);
  decade_counter decade_counter (
    .CLOCK(CLOCK), .CLEAR(or_1_out), .SWITCH(SWITCH), .USER_INPUT(USER_INPUT_0), .OUTPUT(ONES));
  not not_4 (not_4_out, ONES[2]);
  not not_5 (not_5_out, ONES[3]);
  and and_2 (and_2_out, not_5_out, not_4_out, not_6_out, not_7_out);
  not not_6 (not_6_out, ONES[1]);
  not not_7 (not_7_out, ONES[0]);
  or or_1 (or_1_out, and_4_out, CLEAR);
  not not_8 (not_8_out, ONES[1]);
  not not_9 (not_9_out, ONES[0]);
  not not_10 (not_10_out, ONES[3]);
  and and_3 (and_3_out, not_10_out, ONES[2], not_8_out, not_9_out);
  and and_4 (and_4_out, and_1_out, and_3_out);
  Hex_Digit_Display hex_digit_display_1 (.value(TENS));  // open: dp
  Hex_Digit_Display hex_digit_display_2 (.value(ONES));  // open: dp
  Hex_Digit_Display hex_digit_display_3 (.value(USER_INPUT_1));  // open: dp
  Hex_Digit_Display hex_digit_display_4 (.value(USER_INPUT_0));  // open: dp

  // Notes on the sheet:
  //   MOD 24 UP COUNTER
endmodule

module MOD_3_UP_COUNTER (
  input  [3:0] USER_INPUT,
  input  SWITCH,
  input  CLOCK,
  input  CLEAR,
  output [3:0] OUTPUT
);

  wire or_1_out, or_2_out, or_3_out, PARALLEL_LOADING_clear_0, PARALLEL_LOADING_clear_1,
       PARALLEL_LOADING_preset_0, PARALLEL_LOADING_preset_1, t_ff_1_qn;

  Hex_Digit_Display hex_digit_display_1 (.value(USER_INPUT));  // open: dp
  value_set PARALLEL_LOADING (
    .USER_INPUT(USER_INPUT), .SWITCH(SWITCH), .PRESET_1(PARALLEL_LOADING_preset_1),
    .CLEAR_1(PARALLEL_LOADING_clear_1), .PRESET_0(PARALLEL_LOADING_preset_0),
    .CLEAR_0(PARALLEL_LOADING_clear_0));  // open: PRESET_3, CLEAR_3, PRESET_2, CLEAR_2
  or or_1 (or_1_out, OUTPUT[0], OUTPUT[1]);
  T_Flip_Flop t_ff_1 (
    .clk(CLOCK), .T(or_1_out), .Q(OUTPUT[1]), .Qn(t_ff_1_qn), .preset(PARALLEL_LOADING_preset_1),
    .reset(or_2_out), .en(1'b1));
  or or_2 (or_2_out, CLEAR, PARALLEL_LOADING_clear_1);
  T_Flip_Flop t_ff_2 (
    .clk(CLOCK), .T(t_ff_1_qn), .Q(OUTPUT[0]), .preset(PARALLEL_LOADING_preset_0), .reset(or_3_out), .en(1'b1));  // open: Qn
  or or_3 (or_3_out, CLEAR, PARALLEL_LOADING_clear_0);
  not not_1 (OUTPUT[3], 1'b1);
  Hex_Digit_Display hex_digit_display_2 (.value({{2{OUTPUT[3]}}, OUTPUT[1:0]}));  // open: dp

  assign OUTPUT[2] = OUTPUT[3];

  // Notes on the sheet:
  //   MOD 3 UPCOUNTER
endmodule

module _24_HR_CLOCK (
  input  [3:0] HR_1_INPUT,
  input  [3:0] HR_0_INPUT,
  input  [3:0] MIN_1_INPUT,
  input  [3:0] MIN_0_INPUT,
  input  [3:0] SEC_1_INPUT,
  input  [3:0] SEC_0_INPUT,
  input  CLEAR,
  input  SET,
  input  CLOCK,
  output [3:0] HR_1,
  output [3:0] HR_0,
  output [3:0] MIN_1,
  output [3:0] SEC_1,
  output [3:0] MIN_0,
  output [3:0] SEC_0
);

  wire and_1_out, and_2_out, not_1_out, not_2_out, not_3_out, not_4_out, not_5_out, not_6_out, not_7_out,
       not_8_out;

  Hex_Digit_Display hex_digit_display_1 (.value(HR_1));  // open: dp
  MOD_24_UP_COUNTER MOD_24 (
    .CLOCK(and_1_out), .CLEAR(CLEAR), .TENS(HR_1), .ONES(HR_0), .USER_INPUT_1(HR_1_INPUT),
    .USER_INPUT_0(HR_0_INPUT), .SWITCH(SET));
  Hex_Digit_Display hex_digit_display_2 (.value(HR_0));  // open: dp
  Hex_Digit_Display hex_digit_display_3 (.value(MIN_1));  // open: dp
  Hex_Digit_Display hex_digit_display_4 ();  // open: value, dp
  MOD_60_UP_COUNTER MOD_60 (
    .CLOCK(and_2_out), .CLEAR(CLEAR), .TENS(MIN_1), .ONES(MIN_0), .USER_INPUT_1(MIN_1_INPUT),
    .USER_INPUT_0(MIN_0_INPUT), .SWITCH(SET));
  not not_1 (not_1_out, MIN_1[3]);
  not not_2 (not_2_out, MIN_1[1]);
  not not_3 (not_3_out, MIN_1[2]);
  and and_1 (and_1_out, not_1_out, not_3_out, not_2_out, not_4_out);
  Hex_Digit_Display hex_digit_display_5 (.value(MIN_0));  // open: dp
  not not_4 (not_4_out, MIN_1[0]);
  Hex_Digit_Display hex_digit_display_6 (.value(SEC_1));  // open: dp
  Hex_Digit_Display hex_digit_display_7 ();  // open: value, dp
  MOD_60_UP_COUNTER mod_60_up_counter_1 (
    .CLOCK(CLOCK), .CLEAR(CLEAR), .TENS(SEC_1), .ONES(SEC_0), .USER_INPUT_1(SEC_1_INPUT),
    .USER_INPUT_0(SEC_0_INPUT), .SWITCH(SET));
  not not_5 (not_5_out, SEC_1[2]);
  not not_6 (not_6_out, SEC_1[0]);
  not not_7 (not_7_out, SEC_1[3]);
  not not_8 (not_8_out, SEC_1[1]);
  and and_2 (and_2_out, not_7_out, not_5_out, not_8_out, not_6_out);
  Hex_Digit_Display hex_digit_display_8 (.value(SEC_0));  // open: dp
  Hex_Digit_Display hex_digit_display_9 (.value(HR_0_INPUT));  // open: dp
  Hex_Digit_Display hex_digit_display_10 (.value(HR_1_INPUT));  // open: dp
  Hex_Digit_Display hex_digit_display_11 (.value(MIN_1_INPUT));  // open: dp
  Hex_Digit_Display hex_digit_display_12 (.value(MIN_0_INPUT));  // open: dp
  Hex_Digit_Display hex_digit_display_13 (.value(SEC_1_INPUT));  // open: dp
  Hex_Digit_Display hex_digit_display_14 (.value(SEC_0_INPUT));  // open: dp

  // Notes on the sheet:
  //   HR
  //   24 HR CLOCK
  //   MIN
  //   SEC
  //   HR
  //   HR
  //   USER INPUT FOR PARALLEL LOAD
  //   MIN
  //   MIN
  //   SEC
  //   SEC
endmodule

module MOD_30_UP_COUNTER (
  input  CLOCK,
  input  CLEAR,
  input  [3:0] USER_INPUT_1,
  input  [3:0] USER_INPUT_0,
  input  SWITCH,
  output [3:0] TENS,
  output [3:0] ONES
);

  wire and_1_out, not_1_out, not_2_out, not_3_out, not_4_out;

  MOD_3_UP_COUNTER MOD_3_COUNTER (
    .CLOCK(and_1_out), .CLEAR(CLEAR), .SWITCH(SWITCH), .USER_INPUT(USER_INPUT_1), .OUTPUT(TENS));
  decade_counter DECADE_COUNTER (
    .CLOCK(CLOCK), .CLEAR(CLEAR), .SWITCH(SWITCH), .USER_INPUT(USER_INPUT_0), .OUTPUT(ONES));
  not not_1 (not_1_out, ONES[3]);
  not not_2 (not_2_out, ONES[2]);
  not not_3 (not_3_out, ONES[1]);
  and and_1 (and_1_out, not_1_out, not_2_out, not_3_out, not_4_out);
  not not_4 (not_4_out, ONES[0]);
  Hex_Digit_Display hex_digit_display_1 (.value(TENS));  // open: dp
  Hex_Digit_Display hex_digit_display_2 (.value(ONES));  // open: dp
  Hex_Digit_Display hex_digit_display_3 (.value(USER_INPUT_1));  // open: dp
  Hex_Digit_Display hex_digit_display_4 (.value(USER_INPUT_0));  // open: dp

  // Notes on the sheet:
  //   MOD 30 UP COUNTER
endmodule

module TIME_SELECTOR (
  input  [3:0] INPUT_1,
  input  [3:0] INPUT_0,
  output OUTPUT
);

  wire and_1_out, and_2_out, and_3_out, and_4_out, and_5_out, and_6_out, and_7_out, and_8_out, and_9_out,
       and_10_out, not_1_out, not_2_out, not_3_out, not_4_out, not_5_out, not_6_out, not_7_out, not_8_out,
       not_9_out, not_10_out, not_11_out, not_12_out, not_13_out, not_14_out, not_15_out, not_16_out,
       not_17_out;

  not not_1 (not_1_out, INPUT_1[1]);
  not not_2 (not_2_out, INPUT_1[3]);
  not not_3 (not_3_out, INPUT_1[2]);
  and and_1 (and_1_out, not_2_out, not_3_out, not_1_out, INPUT_1[0]);
  not not_4 (not_4_out, INPUT_1[2]);
  not not_5 (not_5_out, INPUT_1[1]);
  not not_6 (not_6_out, INPUT_1[3]);
  and and_2 (and_2_out, not_6_out, not_4_out, not_5_out, not_7_out);
  not not_7 (not_7_out, INPUT_1[0]);
  and and_3 (and_3_out, and_2_out, and_7_out);
  and and_4 (and_4_out, and_1_out, and_10_out);
  or or_1 (OUTPUT, and_3_out, and_4_out, and_6_out, and_9_out);
  not not_8 (not_8_out, INPUT_0[3]);
  and and_5 (and_5_out, not_8_out, INPUT_0[2], INPUT_0[1], INPUT_0[0]);
  and and_6 (and_6_out, and_1_out, and_5_out);
  not not_9 (not_9_out, INPUT_0[2]);
  not not_10 (not_10_out, INPUT_0[1]);
  and and_7 (and_7_out, INPUT_0[3], not_9_out, not_10_out, INPUT_0[0]);
  not not_11 (not_11_out, INPUT_0[1]);
  not not_12 (not_12_out, INPUT_0[0]);
  not not_13 (not_13_out, INPUT_0[2]);
  and and_8 (and_8_out, INPUT_0[3], not_13_out, not_11_out, not_12_out);
  and and_9 (and_9_out, and_1_out, and_8_out);
  not not_14 (not_14_out, INPUT_0[3]);
  not not_15 (not_15_out, INPUT_0[1]);
  not not_16 (not_16_out, INPUT_0[0]);
  not not_17 (not_17_out, INPUT_0[2]);
  and and_10 (and_10_out, not_14_out, not_17_out, not_15_out, not_16_out);
endmodule
