// Logisim project seven.circ as structural Verilog: 9 circuits, main circuit main
module main (
  input  [3:0] in_1,
  input  User_input
);

  wire bl_1_out_2, bot_1_out_2, br_1_out_2, clock_1_out, mid_1_out_2, tl_1_out_2, top_1_out_2, tr_1_out_2;
  wire [3:0] counter_1_out_2, multiplexer_1_out;

  Clock clock_1 (.out(clock_1_out));
  counter counter_1 (.in_1(clock_1_out), .out_2(counter_1_out_2));
  Multiplexer #(.width(4), .enable("false")) multiplexer_1 (
    .in0(counter_1_out_2), .in1(in_1), .out(multiplexer_1_out), .sel(User_input));
  top top_1 (.in_1(multiplexer_1_out), .out_2(top_1_out_2));
  Mid mid_1 (.in_1(multiplexer_1_out), .out_2(mid_1_out_2));
  Bot bot_1 (.in_1(multiplexer_1_out), .out_2(bot_1_out_2));
  TL tl_1 (.in_1(multiplexer_1_out), .out_2(tl_1_out_2));
  BL bl_1 (.in_1(multiplexer_1_out), .out_2(bl_1_out_2));
  TR tr_1 (.in_1(multiplexer_1_out), .out_2(tr_1_out_2));
  BR br_1 (.in_1(multiplexer_1_out), .out_2(br_1_out_2));
  _7_Segment_Display u_7_segment_display_1 (
    .g(mid_1_out_2), .f(tl_1_out_2), .a(top_1_out_2), .b(tr_1_out_2), .e(bl_1_out_2), .d(bot_1_out_2),
    .c(br_1_out_2));  // open: dp
endmodule

// TOP
module top (
  input  [3:0] in_1,
  output out_2
);

  wire and_1_out, and_2_out, not_1_out, not_2_out;

  not not_1 (not_1_out, in_1[2]);
  not not_2 (not_2_out, in_1[0]);
  and and_1 (and_1_out, not_1_out, not_2_out);
  and and_2 (and_2_out, in_1[0], in_1[2]);
  or or_1 (out_2, and_1_out, and_2_out, in_1[3], in_1[1]);
endmodule

// MID
module Mid (
  input  [3:0] in_1,
  output out_2
);

  wire and_1_out, and_2_out, and_3_out, not_1_out, not_2_out, not_3_out;

  not not_1 (not_1_out, in_1[2]);
  not not_2 (not_2_out, in_1[1]);
  not not_3 (not_3_out, in_1[0]);
  and and_1 (and_1_out, in_1[1], not_3_out);
  and and_2 (and_2_out, not_2_out, in_1[2]);
  and and_3 (and_3_out, in_1[1], not_1_out);
  or or_1 (out_2, and_1_out, and_2_out, in_1[3], and_3_out);
endmodule

// BOT
module Bot (
  input  [3:0] in_1,
  output out_2
);

  wire and_1_out, and_2_out, and_3_out, and_4_out, not_1_out, not_2_out, not_3_out;

  not not_1 (not_1_out, in_1[1]);
  not not_2 (not_2_out, in_1[2]);
  not not_3 (not_3_out, in_1[0]);
  and and_1 (and_1_out, not_3_out, not_2_out);
  and and_2 (and_2_out, in_1[1], not_2_out);
  and and_3 (and_3_out, in_1[1], not_3_out);
  and and_4 (and_4_out, in_1[2], not_1_out, in_1[0]);
  or or_1 (out_2, and_1_out, and_2_out, in_1[3], and_3_out, and_4_out);
endmodule

module TL (
  input  [3:0] in_1,
  output out_2
);

  wire and_1_out, and_2_out, and_3_out, not_1_out, not_2_out;

  not not_1 (not_1_out, in_1[0]);
  not not_2 (not_2_out, in_1[1]);
  and and_1 (and_1_out, not_1_out, not_2_out);
  and and_2 (and_2_out, not_2_out, in_1[2]);
  and and_3 (and_3_out, in_1[2], not_1_out);
  or or_1 (out_2, and_1_out, and_2_out, in_1[3], and_3_out);
endmodule

module BL (
  input  [3:0] in_1,
  output out_2
);

  wire and_1_out, and_2_out, and_3_out, and_4_out, not_1_out, not_2_out, or_1_out, or_3_out;

  not not_1 (not_1_out, in_1[2]);
  not not_2 (not_2_out, in_1[0]);
  and and_1 (and_1_out, not_2_out, not_1_out);
  and and_2 (and_2_out, in_1[1], not_2_out);
  and and_3 (and_3_out, in_1[2], in_1[3]);
  and and_4 (and_4_out, in_1[3], in_1[1]);
  or or_1 (or_1_out, and_1_out, and_2_out);
  or or_2 (out_2, or_1_out, or_3_out);
  or or_3 (or_3_out, and_3_out, and_4_out);
endmodule

module TR (
  input  [3:0] in_1,
  output out_2
);

  wire and_1_out, and_2_out, and_3_out, and_4_out, not_1_out, not_2_out, not_3_out, not_4_out;

  not not_1 (not_1_out, in_1[3]);
  not not_2 (not_2_out, in_1[0]);
  not not_3 (not_3_out, in_1[2]);
  not not_4 (not_4_out, in_1[1]);
  and and_1 (and_1_out, not_1_out, not_3_out);
  and and_2 (and_2_out, not_4_out, not_3_out);
  and and_3 (and_3_out, not_1_out, not_4_out, not_2_out);
  and and_4 (and_4_out, not_1_out, in_1[1], in_1[0]);
  or or_1 (out_2, and_1_out, and_2_out, and_3_out, and_4_out);
endmodule

module BR (
  input  [3:0] in_1,
  output out_2
);

  wire and_1_out, and_2_out, and_3_out, not_1_out, not_2_out, not_3_out;

  not not_1 (not_1_out, in_1[1]);
  not not_2 (not_2_out, in_1[3]);
  not not_3 (not_3_out, in_1[2]);
  and and_1 (and_1_out, not_2_out, in_1[0]);
  and and_2 (and_2_out, not_2_out, in_1[2]);
  and and_3 (and_3_out, not_3_out, not_1_out);
  or or_1 (out_2, and_1_out, and_2_out, and_3_out);
endmodule

module counter (
  input  in_1,
  output [3:0] out_2
);

  wire j_k_ff_1_qn, j_k_ff_2_qn, j_k_ff_3_qn;

  J_K_Flip_Flop j_k_ff_1 (.J(1'b1), .clk(in_1), .K(1'b1), .Q(out_2[0]), .Qn(j_k_ff_1_qn));  // open: preset, en, reset
  J_K_Flip_Flop j_k_ff_2 (
    .J(1'b1), .clk(j_k_ff_1_qn), .K(1'b1), .Q(out_2[1]), .Qn(j_k_ff_2_qn));  // open: preset, en, reset
  J_K_Flip_Flop j_k_ff_3 (
    .J(1'b1), .clk(j_k_ff_2_qn), .K(1'b1), .Q(out_2[2]), .Qn(j_k_ff_3_qn));  // open: preset, en, reset
  J_K_Flip_Flop j_k_ff_4 (.J(1'b1), .clk(j_k_ff_3_qn), .K(1'b1), .Q(out_2[3]));  // open: Qn, preset, en, reset
endmodule
